# Fritzing sketch Cercuits Wiring Diagram (saved by Fritzing 0.9.3b)
breadboards: 1

parts:
  U1 = LM2596 step down module
  A1 = Raspberry Pi 5
  J1 = Basic Servo
  A2 = drv-1012
  VCC3 = 4 x AAA Battery Mount
  M2 = DC Motor
  Part1 = VL530X Time of Flight Distance Sensor [part_number="tonetoys #3317"]
  Part2 = VL530X Time of Flight Distance Sensor [part_number="tonetoys #3317"]
  Part4 = VL530X Time of Flight Distance Sensor [part_number="tonetoys #3317"]
  A3 = ESP32 Wroom 32E dev board
  USBTTL1 = USB A Plug
  USBTTL2 = Micro USB B Plug
  Part5 = VL530X Time of Flight Distance Sensor [part_number="tonetoys #3317"]
  Power_plug1 = USB-C plug
  U2 = LM2596 step down module
  Part6 = SparkFun VR IMU Breakout - BNO086 (Qwiic) [part_number=SEN-22857]
  SW1 = Slide_Switch_new
  SW2 = Slide_Switch_new
  IC1 = Rasberry Pi NIOR Camera [chip_label=IC package="DIP (Dual Inline) [THT]"]  # not connected
  IC2 = Rasberry Pi NIOR Camera [chip_label=IC package="DIP (Dual Inline) [THT]"]  # not connected
  IC3 = Rasberry Pi NIOR Camera [chip_label=IC package="DIP (Dual Inline) [THT]"]  # not connected

nets:
  N1: U1.IN+, A2.Pin_12, VCC3.+, U2.IN+
  GND: U1.IN-, U1.OUT-, A1.GND, A1.Fan-GND, J1.gnd, A2.Pin_1, A2.Pin_11, Part1.GND, Part2.GND, Part4.GND, A3.Pin_14, A3.Pin_32, A3.Pin_38, Part5.GND, Power_plug1.GND, U2.IN-, U2.OUT-, Part6.GND, SW1.pin_2, SW2.pin_1
  VCC: U1.OUT+, A2.Pin_5, Part1.VCC, Part2.VCC, Part4.VCC, Part5.VCC
  N2: J1.vcc, U2.OUT+
  N3: J1.pulse, A3.Pin_7
  N4: A2.Pin_3, A3.Pin_11
  N5: A2.Pin_4, A3.Pin_9
  N6: A2.Pin_7, A3.Pin_10
  N7: A2.Pin_8, A3.Pin_8
  N8: A2.Pin_9, M2.pin_1
  N9: A2.Pin_10, M2.pin_2
  N10: VCC3.-, SW1.pin_1
  N11: Part1.SCL, Part2.SCL, Part4.SCL, A3.Pin_36, Part5.SCL, Part6.SCL/SCK/RX
  N12: Part1.SDA, Part2.SDA, Part4.SDA, A3.Pin_33, Part5.SDA, Part6.SDA/MISO/TX
  N13: A3.Pin_1, Part6.3.3V
  N14: A3.Pin_3, SW2.pin_2
  N15: USBTTL1.usb, USBTTL2.usb

custom parts:
  LM2596 step down module: LM2596 DC-DC step down power supply module 3 A.
  Raspberry Pi 5: The RPi5, a faster version of the awesome Raspberry Pi4B ARM Board with 40 pin gpio.
  drv-1012: .The BTS7960 is a fully integrated high current H bridge module for motor drive applications.
  VL530X Time of Flight Distance Sensor: TOF
  ESP32 Wroom 32E dev board: The ESP32 WROOM-32E is a versatile and powerful module built around Espressif’s ESP32 chipset. It offers dual-core processing, integrated Wi-Fi and Bluetooth connectivity, and boasts a wide range of peripheral interfaces.
  USB-C plug: power plug
  SparkFun VR IMU Breakout - BNO086 (Qwiic): Virtual reality is in, but you shouldn't have to drop hundreds of dollars to gain access to the technology behind it. Luckily, that's where the SparkFun VR IMU Breakout comes in. At its heart is CEVA’s BNO086, a combination triple-axis accelerometer/gyro/magnetometer System in Package (SiP) with a 32-bit ARM© Cortex™ M0+. The BNO086 Inertial Measurement Unit (IMU) produces accurate rotation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
  Slide_Switch_new: the New two pin slide switch
  Rasberry Pi NIOR Camera: Camera
